# Fritzing sketch LanguageDetection (saved by Fritzing 0.9.6b)

parts:
  Arduino_Nano_33_BLE_Sense = Arduino Nano 33 BLE Sense
  Servos_03 = Basic Servo
  Servos_02 = Basic Servo
  Servos_01 = Basic Servo
  pca9685 = 16-Channel 12-bit PCA9685 PWM/Servo Driver
  part = Battery block 9V

nets:
  +5V: Arduino_Nano_33_BLE_Sense.D11/MOSI, Arduino_Nano_33_BLE_Sense.+5V, pca9685.VCC
  GND: Arduino_Nano_33_BLE_Sense.GND, Servos_03.gnd, Servos_02.gnd, Servos_01.gnd, pca9685.GND, part.-
  N1: Arduino_Nano_33_BLE_Sense.A5, pca9685.SCL
  N2: Arduino_Nano_33_BLE_Sense.A4, pca9685.SDA
  VCC: Servos_03.vcc, Servos_02.vcc, Servos_01.vcc, pca9685.V+
  N3: Servos_03.pulse, pca9685.2
  N4: Servos_02.pulse, pca9685.1
  N5: Servos_01.pulse, pca9685.0
  N6: pca9685.PWRIN, part.+

custom parts:
  Arduino Nano 33 BLE Sense: The Nano 33 BLE Sense (without headers) is Arduino’s 3.3V AI enabled board in the smallest available form factor: 45x18mm! The Arduino Nano 33 BLE Sense is a completely new board on a well-known form factor. It comes with a series of embedded sensors: 9 axis inertial sensor: what makes this board ideal for wearable devices humidity, and temperature sensor: to get highly accurate measurements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
  16-Channel 12-bit PCA9685 PWM/Servo Driver: The Adafruit 16-Channel 12-bit PWM/Servo Driver will drive up to 16 servos over I2C with only 2 pins. The on-board PCA9685 PWM controller will drive all 16 channels simultaneously with no additional processing overhead. What's more, you can chain up to 62 of them to control up to 992 servos - all with the same 2 pins
