# Fritzing sketch water_timer (saved by Fritzing 0.9.4)
circuit board: 4.86967cm x 5.40558cm
breadboards: 1

parts:
  part = Arduino Nano 33 BLE Sense
  2N222 = TRANSISTOR_NPN [package=to-92]
  buzzer = Piezo Speaker
  6V = 4 x AAA Battery Mount
  LED1 = LEDs [package=led10mm]

nets:
  N1: part.GND, 2N222.C, 6V.-, LED1.C
  N2: part.D2, 2N222.B
  N3: part.D3~, LED1.A
  N4: 2N222.E, buzzer.pin1
  N5: buzzer.pin2, 6V.+

custom parts:
  Arduino Nano 33 BLE Sense: The Nano 33 BLE Sense (without headers) is Arduino’s 3.3V AI enabled board in the smallest available form factor: 45x18mm! The Arduino Nano 33 BLE Sense is a completely new board on a well-known form factor. It comes with a series of embedded sensors: 9 axis inertial sensor: what makes this board ideal for wearable devices humidity, and temperature sensor: to get highly accurate measurements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
