# Fritzing sketch rasberry_elletric (saved by Fritzing 0.9.4)

parts:
  Raspberry_Pi_1 = Raspberry Pi 3 [part_number=RPI-3-V1.2]
  Part1 = 16-Channel 12-bit PCA9685 PWM/Servo Driver
  J1 = Basic Servo
  J2 = Basic Servo
  J3 = Basic Servo
  VCC1 = Battery block 9V

nets:
  3V3: Raspberry_Pi_1.3v3, Part1.VCC
  N1: Raspberry_Pi_1.GPIO2, Part1.SDA
  N2: Raspberry_Pi_1.GPIO3, Part1.SCL
  GND: Raspberry_Pi_1.GND, Part1.GND, J1.gnd, J2.gnd, J3.gnd, VCC1.-
  N3: Part1.PWRIN, VCC1.+
  N4: Part1.0, J3.pulse
  N5: Part1.1, J2.pulse
  N6: Part1.3, J1.pulse
  VCC: Part1.V+, J1.vcc, J2.vcc, J3.vcc

custom parts:
  16-Channel 12-bit PCA9685 PWM/Servo Driver: The Adafruit 16-Channel 12-bit PWM/Servo Driver will drive up to 16 servos over I2C with only 2 pins. The on-board PCA9685 PWM controller will drive all 16 channels simultaneously with no additional processing overhead. What's more, you can chain up to 62 of them to control up to 992 servos - all with the same 2 pins
